# Fritzing sketch Transistor_NOT_and_AMP (saved by Fritzing 0.9.1b)
breadboards: 1

parts:
  Componente1 = Arduino Uno (Rev3)
  Q1 = NPN-Transistor [package="TO92 [THT]"]
  Q2 = NPN-Transistor [package="TO92 [THT]"]
  Q3 = NPN-Transistor [package="TO92 [THT]"]
  Q4 = NPN-Transistor [package="TO92 [THT]"]
  LED1 = LED - 5mm [color="Green (570nm)" package="5 mm [THT]"]
  R1 = Resistor [tolerance=±5% resistance=220 package=THT]
  Q5 = NPN-Transistor [package="TO92 [THT]"]
  R2 = Resistor [tolerance=±5% resistance=220 package=THT]
  LED2 = LED - 5mm [color="Yellow (592nm)" package="5 mm [THT]"]

nets:
  N1: Componente1.D13/SCK, Q1.B, Q4.B
  N2: Componente1.5V, Q1.E, Q2.E, Q3.E, Q4.E, R2.Pin_0
  N3: Componente1.GND, R1.Pin_0, Q5.C, LED2.cathode
  N4: Q1.C, Q2.B
  N5: Q2.C, Q3.B
  N6: Q3.C, Q5.B
  N7: Q4.C, LED1.anode
  N8: LED1.cathode, R1.Pin_1
  N9: Q5.E, R2.Pin_1, LED2.anode
