# Fritzing sketch fritz_Button_Serial (saved by Fritzing 0.9.1b)
breadboards: 1

parts:
  ArduinoUNO = Arduino Uno (Rev3)
  S1 = Pushbutton [package="[THT]"]
  R1 = Resistor [tolerance=±5% resistance=10k package=THT]
  R2 = Resistor [tolerance=±5% resistance=220 package=THT]
  LED1 = LED - 5mm [color="Red (633nm)" package="5 mm [THT]"]
  LED2 = LED - 5mm [color="Green (570nm)" package="5 mm [THT]"]
  R3 = Resistor [tolerance=±5% resistance=220 package=THT]

nets (from the schematic view):
  N1: ArduinoUNO.D8, R3.Pin_0
  N2: ArduinoUNO.D2, S1.Pin_1, S1.Pin_2, R2.Pin_0
  N3: ArduinoUNO.5V, S1.Pin_3, S1.Pin_4, R1.Pin_1
  N4: ArduinoUNO.GND, R1.Pin_0, LED1.cathode, LED2.cathode
  N5: R2.Pin_1, LED1.anode
  N6: LED2.anode, R3.Pin_1
