# Fritzing sketch buzzer (saved by Fritzing 0.9.1b)
breadboards: 1

parts:
  Componente1 = Arduino Uno (Rev3)
  R1 = Rotary Potentiometer (Small) [maximum_resistance=100kΩ package=THT]
  LED1 = LED - 5mm [color="Red (633nm)" package="5 mm [THT]"]
  J1 = Piezo Speaker

nets:
  N1: Componente1.GND, R1.leg2, J1.pin1
  N2: Componente1.D2, R1.leg1
  N3: R1.wiper, LED1.anode
  N4: LED1.cathode, J1.pin2
