# Fritzing sketch sketch_fotoresistenza (saved by Fritzing 0.9.1b)
breadboards: 1

parts:
  Componente1 = Arduino Uno (Rev3)
  R1 = Photocell (LDR) [package=THT]
  R2 = Resistor [tolerance=±5% resistance=10k package=THT]
  LED1 = LED - 5mm [color="Green (555nm)" package="5 mm [THT]"]
  LED3 = LED - 5mm [color="Red (633nm)" package="5 mm [THT]"]
  R3 = Resistor [tolerance=±5% resistance=220 package=THT]
  R4 = Resistor [tolerance=±5% resistance=220 package=THT]
  R5 = Resistor [tolerance=±5% resistance=220 package=THT]
  LED2 = smd LED [color="Yellow (585nm)" package="0805 [SMD]"]

nets:
  N1: Componente1.A0, R1.pin_0, R2.Pin_1
  N2: Componente1.D2, R3.Pin_1
  N3: Componente1.D4, R4.Pin_1
  N4: Componente1.D7, R5.Pin_1
  N5: Componente1.5V, R1.pin_1
  N6: Componente1.GND, R2.Pin_0, LED1.cathode, LED3.cathode, LED2.cathode
  N7: LED1.anode, R5.Pin_0
  N8: LED3.anode, R3.Pin_0
  N9: R4.Pin_0, LED2.anode
