# Fritzing sketch ledRGB_AnodoComune (saved by Fritzing 0.9.1b)
breadboards: 1

parts:
  Componente1 = Arduino Uno (Rev3)
  Q1 = NPN-Transistor [package="TO92 [THT]"]
  R1 = Resistor [tolerance=±5% resistance=220 package=THT]
  LED1 = RGB LED (com. anode, rbg) [package="5 mm [THT]"]
  R2 = Resistor [tolerance=±5% resistance=220 package=THT]
  Q2 = NPN-Transistor [package="TO92 [THT]"]
  R3 = Resistor [tolerance=±5% resistance=220 package=THT]
  Q3 = NPN-Transistor [package="TO92 [THT]"]
  R4 = Resistor [tolerance=±5% resistance=220 package=THT]

nets:
  N1: Componente1.D9_PWM, Q1.B, R1.Pin_0
  N2: Componente1.D10_PWM/SS, Q2.B, R3.Pin_0
  N3: Componente1.D11_PWM/MOSI, Q3.B, R4.Pin_0
  N4: Q1.E, LED1.green_cathode
  N5: Q1.C, Q2.C, Q3.C
  N6: R1.Pin_1, R2.Pin_1, R3.Pin_1, R4.Pin_1
  N7: LED1.red_cathode, Q3.E
  N8: LED1.common_anode, Q2.E
  N9: LED1.blue_cathode, R2.Pin_0
