# Fritzing sketch fritzing_potenziometro (saved by Fritzing 0.9.1b)
breadboards: 1

parts:
  Componente1 = Arduino Uno (Rev3)
  R1 = Trimmer Potentiometer [maximum_resistance=10kΩ package=THT]
  R2 = Resistor [tolerance=±5% resistance=220 package=THT]
  LED1 = LED - 5mm [color="Red (633nm)" package="5 mm [THT]"]
  R3 = Resistor [tolerance=±5% resistance=220 package=THT]
  R4 = Resistor [tolerance=±5% resistance=220 package=THT]
  R5 = Resistor [tolerance=±5% resistance=220 package=THT]
  LED2 = LED - 5mm [color="Red (633nm)" package="5 mm [THT]"]
  LED3 = LED - 5mm [color="Yellow (574nm)" package="5 mm [THT]"]
  LED4 = LED - 5mm [color="Green (555nm)" package="5 mm [THT]"]

nets (from the schematic view):
  N1: Componente1.A0, R1.leg2, R2.Pin_1
  N2: Componente1.GND, R1.wiper, LED2.cathode, LED3.cathode, LED4.cathode
  N3: Componente1.D2, R3.Pin_0
  N4: Componente1.D4, R4.Pin_0
  N5: Componente1.D7, R5.Pin_0
  N6: Componente1.5V, R1.leg1
  N7: R2.Pin_0, LED1.anode
  N8: R3.Pin_1, LED2.anode
  N9: R4.Pin_1, LED3.anode
  N10: R5.Pin_1, LED4.anode
