# Fritzing sketch supercar (saved by Fritzing 0.9.1b)
breadboards: 1

parts:
  R1 = Resistor [tolerance=±5% resistance=220 package=THT]
  R2 = Resistor [tolerance=±5% resistance=220 package=THT]
  R3 = Resistor [tolerance=±5% resistance=220 package=THT]
  R4 = Resistor [tolerance=±5% resistance=220 package=THT]
  R5 = Resistor [tolerance=±5% resistance=220 package=THT]
  R6 = Resistor [tolerance=±5% resistance=220 package=THT]
  R7 = Resistor [tolerance=±5% resistance=220 package=THT]
  R8 = Resistor [tolerance=±5% resistance=220 package=THT]
  LED1 = LED - 5mm [color="Red (633nm)" package="5 mm [THT]"]
  LED2 = LED - 5mm [color="Red (633nm)" package="5 mm [THT]"]
  LED3 = LED - 5mm [color="Red (633nm)" package="5 mm [THT]"]
  LED4 = LED - 5mm [color="Red (633nm)" package="5 mm [THT]"]
  LED5 = LED - 5mm [color="Red (633nm)" package="5 mm [THT]"]
  LED6 = LED - 5mm [color="Red (633nm)" package="5 mm [THT]"]
  LED7 = LED - 5mm [color="Red (633nm)" package="5 mm [THT]"]
  LED8 = LED - 5mm [color="Red (633nm)" package="5 mm [THT]"]
  R9 = Resistor [tolerance=±5% resistance=220 package=THT]
  R10 = Resistor [tolerance=±5% resistance=220 package=THT]
  LED9 = LED - 5mm [color="Red (633nm)" package="5 mm [THT]"]
  LED10 = LED - 5mm [color="Red (633nm)" package="5 mm [THT]"]
  R11 = Rotary Potentiometer (Small) [maximum_resistance=100kΩ package=THT]
  Componente1 = Arduino Uno (Rev3) - ICSP

nets:
  N1: R1.Pin_0, LED1.anode
  N2: R1.Pin_1, Componente1.D1/TX
  N3: R2.Pin_0, LED2.anode
  N4: R2.Pin_1, Componente1.D2
  N5: R3.Pin_0, LED3.anode
  N6: R3.Pin_1, Componente1.D3_PWM
  N7: R4.Pin_0, LED4.anode
  N8: R4.Pin_1, Componente1.D4
  N9: R5.Pin_0, LED5.anode
  N10: R5.Pin_1, Componente1.D5_PWM
  N11: R6.Pin_0, LED6.anode
  N12: R6.Pin_1, Componente1.D6_PWM
  N13: R7.Pin_0, LED7.anode
  N14: R7.Pin_1, Componente1.D7
  N15: R8.Pin_0, LED8.anode
  N16: R8.Pin_1, Componente1.D8
  N17: LED1.cathode, LED2.cathode, LED3.cathode, LED4.cathode, LED5.cathode, LED6.cathode, LED7.cathode, LED8.cathode, LED9.cathode, LED10.cathode, R11.leg1, Componente1.GND
  N18: R9.Pin_0, LED9.anode
  N19: R9.Pin_1, Componente1.D9_PWM
  N20: R10.Pin_0, LED10.anode
  N21: R10.Pin_1, Componente1.D10_PWM/SS
  N22: R11.wiper, Componente1.A0
  N23: R11.leg2, Componente1.5V
